// Logisim project CS1404_U201414667_甘鹏_MIPS_CPU.circ as structural Verilog: 5 circuits, main circuit main
module main (
);

  wire ALUSrc, and_4_out, and_5_out, and_6_out, beq, bgez, bne, clk, clock_1_out, comparator_1_eq,
       comparator_2_eq, comparator_3_eq, equal, halt, j, jal, jr, MemRead, MemtoReg, MemWrite, not_1_out,
       not_2_out, or_1_out, or_2_out, RegDst, RegWrite, sb, Shamt_Sign, Sign, srav, systemcall;
  wire [3:0] ALUop;
  wire [4:0] bit_extender_4_out, multiplexer_1_out, multiplexer_2_out, multiplexer_4_out, multiplexer_5_out,
       multiplier_1_out, rd, rs, rt, shamt;
  wire [5:0] funct, OP;
  wire [15:0] imme;
  wire [25:0] addr;
  wire [31:0] a0, adder_2_out, alu_1_result, and_3_out, and_7_out, bit_extender_1_out, bit_extender_2_out,
       bit_extender_3_out, bit_extender_5_out, I_imm, main_1_s0_value, main_1_s1_value, main_1_s2_value,
       multiplexer_3_out, multiplexer_6_out, multiplexer_8_out, multiplexer_9_out, multiplexer_10_out,
       multiplexer_11_out, multiplexer_12_out, multiplexer_13_out, multiplexer_14_out, multiplexer_15_out,
       multiplexer_16_out, multiplexer_17_out, multiplexer_18_out, or_3_out, pc4, PC_2_q, PC_q, ra,
       ram_1_data, register_2_q, rom_1_data, shifter_1_out, shifter_2_out, v0;

  Clock clock_1 (.out(clock_1_out));
  // Probe on PC_q
  Counter #(.width(32), .max('hffffffff)) PC (.Q(PC_q), .clk(clk));  // open: load, D, count, carry, clr
  and and_1 (clk, clock_1_out, ~halt);  // AND_Gate
  Control_Unit control_unit_1 (
    .op(OP), .funct(funct), .RegDst(RegDst), .ALUop(ALUop), .RegWrite(RegWrite), .Sign(Sign),
    .Shamt_Sign(Shamt_Sign), .MemRead(MemRead), .MemWrite(MemWrite), .MemtoReg(MemtoReg), .ALUSrc(ALUSrc),
    .beq(beq), .bne(bne), .j(j), .jal(jal), .jr(jr), .srav(srav), .bgez(bgez), .sb(sb));
  Register #(.width(32)) PC_2 (.D(multiplexer_15_out), .Q(PC_2_q), .clk(clk));  // open: en, clr
  Adder #(.width(32)) adder_1 (.a(PC_2_q), .b(32'h4), .out(pc4));  // open: cin, cout
  // Probe on main_1_s0_value
  Multiplexer #(.width(5), .enable("false")) multiplexer_1 (
    .in0(rs), .in1(5'b00010), .out(multiplexer_1_out), .sel(systemcall));
  Multiplexer #(.width(5), .enable("false")) multiplexer_2 (
    .in0(rt), .in1(5'b00100), .out(multiplexer_2_out), .sel(systemcall));
  Multiplexer #(.width(32), .enable("false")) multiplexer_3 (
    .in0({32{1'b0}}), .in1(v0), .out(multiplexer_3_out), .sel(systemcall));
  // Probe on main_1_s1_value
  Multiplexer #(.width(5), .enable("false")) multiplexer_4 (.in0(rt), .in1(rd), .out(multiplexer_4_out), .sel(RegDst));
  Comparator #(.width(32)) comparator_1 (.a(multiplexer_3_out), .b(32'ha), .eq(comparator_1_eq));  // open: gt, lt
  ROM #(.addrWidth(10), .dataWidth(32)) rom_1 (.addr(PC_2_q[11:2]), .data(rom_1_data));  // open: sel
  // Probe on main_1_s2_value
  Multiplexer #(.width(5), .enable("false")) multiplexer_5 (
    .in0(multiplexer_4_out), .in1({5{1'b1}}), .out(multiplexer_5_out), .sel(jal));
  Multiplexer #(.width(32), .enable("false")) multiplexer_6 (
    .in0(multiplexer_18_out), .in1(pc4), .out(multiplexer_6_out), .sel(jal));
  assign bit_extender_1_out = {{16{1'b0}}, imme};  // Bit_Extender bit_extender_1
  Multiplexer #(.width(32), .enable("false")) multiplexer_7 (
    .in0(bit_extender_1_out), .in1(bit_extender_2_out), .out(I_imm), .sel(Sign));
  assign bit_extender_2_out = {{16{imme[15]}}, imme};  // Bit_Extender bit_extender_2
  Register #(.width(1)) register_1 (.D(comparator_1_eq), .Q(halt), .clk(clk));  // open: en, clr
  Decoder decoder_1 (
    .instruction(rom_1_data), .func(funct), .shamt(shamt), .rd(rd), .rt(rt), .rs(rs), .op(OP), .I_imed(imme),
    .J_imed(addr));
  \CS1404_U201414667_甘鹏_regfile_main  main_1 (
    .Reg1_num(multiplexer_1_out), .Reg2(multiplexer_2_out), .Write_Reg_num(multiplexer_5_out),
    .Din(multiplexer_6_out), .Write_Enable(RegWrite), .Clock(clk), .Reg1(v0), .Reg2_2(a0),
    .s0_Value(main_1_s0_value), .s1_Value(main_1_s1_value), .s2_Value(main_1_s2_value), .ra_Value(ra));
  Register #(.width(32)) register_2 (.D(a0), .Q(register_2_q), .clk(not_1_out));  // open: en, clr
  not not_1 (not_1_out, systemcall);
  Multiplexer #(.width(32), .enable("false")) multiplexer_8 (
    .in0(a0), .in1(I_imm), .out(multiplexer_8_out), .sel(ALUSrc));
  assign bit_extender_3_out = {{27{1'b0}}, shamt};  // Bit_Extender bit_extender_3
  Hex_Digit_Display hex_digit_display_1 (.value(register_2_q[27:24]));  // open: dp
  Hex_Digit_Display hex_digit_display_2 (.value(register_2_q[31:28]));  // open: dp
  Multiplexer #(.width(32), .enable("false")) multiplexer_9 (
    .in0(v0), .in1(a0), .out(multiplexer_9_out), .sel(Shamt_Sign));
  Multiplexer #(.width(32), .enable("false")) multiplexer_10 (
    .in0(multiplexer_8_out), .in1(bit_extender_3_out), .out(multiplexer_10_out), .sel(Shamt_Sign));
  Hex_Digit_Display hex_digit_display_3 (.value(register_2_q[23:20]));  // open: dp
  Hex_Digit_Display hex_digit_display_4 (.value(register_2_q[19:16]));  // open: dp
  Comparator #(.width(6)) comparator_2 (.a(OP), .b({6{1'b0}}), .eq(comparator_2_eq));  // open: gt, lt
  and and_2 (systemcall, comparator_2_eq, comparator_3_eq);
  Comparator #(.width(6)) comparator_3 (.a(funct), .b(6'b001100), .eq(comparator_3_eq));  // open: gt, lt
  assign and_3_out = v0 & 32'h1f;  // AND_Gate and_3, 32 bits wide
  Hex_Digit_Display hex_digit_display_5 (.value(register_2_q[15:12]));  // open: dp
  Hex_Digit_Display hex_digit_display_6 (.value(register_2_q[11:8]));  // open: dp
  Shifter #(.width(32)) shifter_1 (.in(I_imm), .\dist (5'b00010), .out(shifter_1_out));
  and and_4 (and_4_out, beq, equal);
  and and_5 (and_5_out, ~equal, bne);  // AND_Gate
  Multiplexer #(.width(32), .enable("false")) multiplexer_11 (
    .in0(multiplexer_10_out), .in1(and_3_out), .out(multiplexer_11_out), .sel(srav));
  Hex_Digit_Display hex_digit_display_7 (.value(register_2_q[7:4]));  // open: dp
  Hex_Digit_Display hex_digit_display_8 (.value(register_2_q[3:0]));  // open: dp
  Adder #(.width(32)) adder_2 (.a(pc4), .b(shifter_1_out), .out(adder_2_out));  // open: cin, cout
  Multiplexer #(.width(32), .enable("false")) multiplexer_12 (
    .in0(multiplexer_11_out), .in1({32{1'b0}}), .out(multiplexer_12_out), .sel(bgez));
  Multiplexer #(.width(32), .enable("false")) multiplexer_13 (
    .in0(pc4), .in1(adder_2_out), .out(multiplexer_13_out), .sel(or_2_out));
  Multiplexer #(.width(32), .enable("false")) multiplexer_14 (
    .in0(multiplexer_13_out), .in1({pc4[31:28], addr, 2'b00}), .out(multiplexer_14_out), .sel(or_1_out));
  or or_1 (or_1_out, j, jal);
  or or_2 (or_2_out, and_4_out, and_6_out, and_5_out);
  and and_6 (and_6_out, bgez, not_2_out);
  not not_2 (not_2_out, alu_1_result[0]);
  ALU alu_1 (
    .AluOP(ALUop), .X(multiplexer_9_out), .Equal(equal), .Result(alu_1_result), .Y(multiplexer_12_out));  // open: Signed_Overflow, Result_2, UnSigned_Overflow
  Multiplexer #(.width(32), .enable("false")) multiplexer_15 (
    .in0(multiplexer_14_out), .in1(v0), .out(multiplexer_15_out), .sel(jr));
  assign bit_extender_4_out = {{3{1'b0}}, alu_1_result[1:0]};  // Bit_Extender bit_extender_4
  Multiplexer #(.width(32), .enable("false")) multiplexer_16 (
    .in0(a0), .in1(or_3_out), .out(multiplexer_16_out), .sel(sb));
  Multiplier #(.width(5)) multiplier_1 (
    .a(bit_extender_4_out), .b(5'b01000), .out(multiplier_1_out));  // open: cin, cout
  assign or_3_out = shifter_2_out | and_7_out;  // OR_Gate or_3, 32 bits wide
  // Probe on addr
  // Probe on OP
  // Probe on rs
  // Probe on rt
  // Probe on rd
  // Probe on shamt
  // Probe on imme
  // Probe on funct
  assign bit_extender_5_out = {{24{1'b0}}, a0[7:0]};  // Bit_Extender bit_extender_5
  assign and_7_out = ram_1_data & multiplexer_17_out;  // AND_Gate and_7, 32 bits wide
  RAM #(.addrWidth(10), .dataWidth(32), .bus("separate")) ram_1 (
    .addr(alu_1_result[11:2]), .din(multiplexer_16_out), .data(ram_1_data), .str(MemWrite), .clk(clk),
    .ld(MemRead));  // open: sel, clr
  Shifter #(.width(32)) shifter_2 (.in(bit_extender_5_out), .\dist (multiplier_1_out), .out(shifter_2_out));
  Multiplexer #(.select(2), .width(32), .enable("false")) multiplexer_17 (
    .in0(32'hffffff00), .in1(32'hffff00ff), .in2(32'hff00ffff), .in3(32'hffffff), .out(multiplexer_17_out),
    .sel(alu_1_result[1:0]));
  Multiplexer #(.width(32), .enable("false")) multiplexer_18 (
    .in0(alu_1_result), .in1(ram_1_data), .out(multiplexer_18_out), .sel(MemtoReg));

  // Other names for the same wires on the sheet: Din[31:0] = a0

  // Notes on the sheet:
  //   contents of rom_1 (hex, n*v repeats v):
  //   20100001 20110001 2308007 22310003 2308007 2e300001 20110000 2e300001 20110003 20100000 a2110000
  //   a2110001 a2110002 a2110003 a2110004 2010ffff 601fff7 20100000 601fff5
endmodule

module Control_Unit (
  input  [5:0] op,
  input  [5:0] funct,
  output RegDst,
  output [3:0] ALUop,
  output RegWrite,
  output Sign,
  output Shamt_Sign,
  output MemRead,
  output MemWrite,
  output MemtoReg,
  output ALUSrc,
  output beq,
  output bne,
  output j,
  output jal,
  output jr,
  output srav,
  output bgez,
  output sb
);

  wire add, addi, addiu, addu, \and , andi, \nor , \or , ori, sll, slt, slti, sltiu, sltu, sra, srl, sub, sw;

  I_type i_type_1 (
    .op5(op[5]), .op4(op[4]), .op3(op[3]), .op2(op[2]), .op1(op[1]), .op0(op[0]), .addi(addi), .addiu(addiu),
    .andi(andi), .ori(ori), .lw(MemtoReg), .sw(sw), .beq(beq), .bne(bne), .slti(slti), .j(j), .jal(jal),
    .fenable(RegDst), .sltiu(sltiu), .sb(sb), .bgez(bgez));
  R_type r_type_1 (
    .fenable(RegDst), .funct5(funct[5]), .funct4(funct[4]), .funct3(funct[3]), .funct2(funct[2]),
    .funct1(funct[1]), .funct0(funct[0]), .add(add), .addu(addu), .\and (\and ), .sll(sll), .sra(sra),
    .srl(srl), .sub(sub), .\or (\or ), .\nor (\nor ), .slt(slt), .sltu(sltu), .jr(jr), .srav(srav));
  or or_1 (RegWrite, sltiu, add, addu, \and , sll, sra, srl, sub, \or , \nor , sltu, addi, addiu, andi, ori, MemtoReg, slti, slt, jal, srav);
  or or_2 (Sign, sb, addi, MemtoReg, sw, beq, bne, slti, bgez);
  or or_3 (Shamt_Sign, sll, sra, srav, srl);
  or or_4 (ALUSrc, sltiu, addi, addiu, andi, ori, MemtoReg, sw, slti, sb);
  or or_5 (ALUop[3], sltiu, \or , ori, \nor , slt, slti, sltu, bgez);
  or or_6 (ALUop[2], sltiu, add, addi, addu, addiu, \and , sub, andi, MemtoReg, sw, sltu, sb);
  or or_7 (ALUop[1], bgez, andi, sub, \nor , slt, slti, srl, \and );
  or or_8 (ALUop[0], bgez, srav, addi, addu, addiu, \and , andi, sra, slti, MemtoReg, sw, slt, add, sb);
  or or_9 (MemRead, MemtoReg, sb);
  or or_10 (MemWrite, sb, sw);

  // Other names for the same wires on the sheet: lw = MemtoReg
endmodule

module Decoder (
  input  [31:0] instruction,
  output [5:0] func,
  output [4:0] shamt,
  output [4:0] rd,
  output [4:0] rt,
  output [4:0] rs,
  output [5:0] op,
  output [15:0] I_imed,
  output [25:0] J_imed
);


  assign func = instruction[5:0];
  assign I_imed = instruction[15:0];
  assign J_imed = instruction[25:0];
  assign op = instruction[31:26];
  assign rd = instruction[15:11];
  assign rs = instruction[25:21];
  assign rt = instruction[20:16];
  assign shamt = instruction[10:6];
endmodule

module I_type (
  input  op5,
  input  op4,
  input  op3,
  input  op2,
  input  op1,
  input  op0,
  output addi,
  output addiu,
  output andi,
  output ori,
  output lw,
  output sw,
  output beq,
  output bne,
  output slti,
  output j,
  output jal,
  output sltiu,
  output sb,
  output bgez,
  output fenable
);

  wire not_1_out, not_2_out, not_3_out, not_4_out, not_5_out, not_6_out, not_7_out, not_8_out, not_9_out,
       not_10_out, not_11_out, not_12_out, not_13_out, not_14_out, not_15_out, not_16_out, not_17_out,
       not_18_out, not_19_out, not_20_out, not_21_out, not_22_out, not_23_out, not_24_out, not_25_out,
       not_26_out, not_27_out, not_28_out, not_29_out, not_30_out, not_31_out, not_32_out, not_33_out,
       not_34_out, not_35_out, not_36_out, not_37_out, not_38_out, not_39_out, not_40_out, not_41_out,
       not_42_out, not_43_out, not_44_out, not_45_out, not_46_out, not_47_out, not_48_out, not_49_out,
       not_50_out, not_51_out, not_52_out, not_53_out, not_54_out, not_55_out, not_56_out, not_57_out,
       not_58_out, not_59_out, not_60_out, not_61_out;

  not not_1 (not_1_out, op5);
  not not_2 (not_2_out, op4);
  not not_3 (not_3_out, op2);
  not not_4 (not_4_out, op1);
  not not_5 (not_5_out, op0);
  not not_6 (not_6_out, op5);
  not not_7 (not_7_out, op4);
  not not_8 (not_8_out, op2);
  not not_9 (not_9_out, op1);
  not not_10 (not_10_out, op5);
  not not_11 (not_11_out, op4);
  not not_12 (not_12_out, op1);
  not not_13 (not_13_out, op0);
  not not_14 (not_14_out, op5);
  not not_15 (not_15_out, op4);
  not not_16 (not_16_out, op1);
  not not_17 (not_17_out, op4);
  not not_18 (not_18_out, op3);
  not not_19 (not_19_out, op2);
  not not_20 (not_20_out, op4);
  not not_21 (not_21_out, op2);
  not not_22 (not_22_out, op5);
  not not_23 (not_23_out, op4);
  not not_24 (not_24_out, op3);
  not not_25 (not_25_out, op1);
  not not_26 (not_26_out, op0);
  not not_27 (not_27_out, op5);
  not not_28 (not_28_out, op4);
  not not_29 (not_29_out, op3);
  not not_30 (not_30_out, op1);
  not not_31 (not_31_out, op5);
  not not_32 (not_32_out, op4);
  not not_33 (not_33_out, op2);
  not not_34 (not_34_out, op0);
  not not_35 (not_35_out, op5);
  not not_36 (not_36_out, op4);
  not not_37 (not_37_out, op3);
  not not_38 (not_38_out, op2);
  not not_39 (not_39_out, op0);
  not not_40 (not_40_out, op5);
  not not_41 (not_41_out, op4);
  not not_42 (not_42_out, op3);
  not not_43 (not_43_out, op2);
  not not_44 (not_44_out, op5);
  not not_45 (not_45_out, op4);
  not not_46 (not_46_out, op2);
  not not_47 (not_47_out, op4);
  not not_48 (not_48_out, op2);
  not not_49 (not_49_out, op1);
  not not_50 (not_50_out, op0);
  not not_51 (not_51_out, op5);
  not not_52 (not_52_out, op4);
  not not_53 (not_53_out, op3);
  not not_54 (not_54_out, op2);
  not not_55 (not_55_out, op1);
  not not_56 (not_56_out, op5);
  not not_57 (not_57_out, op4);
  not not_58 (not_58_out, op3);
  not not_59 (not_59_out, op2);
  not not_60 (not_60_out, op1);
  not not_61 (not_61_out, op0);
  and and_1 (addi, not_1_out, not_2_out, op3, not_3_out, not_4_out, not_5_out);
  and and_2 (addiu, not_6_out, not_7_out, op3, not_8_out, not_9_out, op0);
  and and_3 (andi, not_10_out, not_11_out, op3, op2, not_12_out, not_13_out);
  and and_4 (ori, not_14_out, not_15_out, op3, op2, not_16_out, op0);
  and and_5 (lw, op5, not_17_out, not_18_out, not_19_out, op1, op0);
  and and_6 (sw, op5, not_20_out, op3, not_21_out, op1, op0);
  and and_7 (beq, not_22_out, not_23_out, not_24_out, op2, not_25_out, not_26_out);
  and and_8 (bne, not_27_out, not_28_out, not_29_out, op2, not_30_out, op0);
  and and_9 (slti, not_31_out, not_32_out, op3, not_33_out, op1, not_34_out);
  and and_10 (j, not_35_out, not_36_out, not_37_out, not_38_out, op1, not_39_out);
  and and_11 (jal, not_40_out, not_41_out, not_42_out, not_43_out, op1, op0);
  and and_12 (sltiu, not_44_out, not_45_out, op3, not_46_out, op1, op0);
  and and_13 (sb, op5, not_47_out, op3, not_48_out, not_49_out, not_50_out);
  and and_14 (bgez, not_51_out, not_52_out, not_53_out, not_54_out, not_55_out, op0);
  and and_15 (fenable, not_56_out, not_57_out, not_58_out, not_59_out, not_60_out, not_61_out);
endmodule

module R_type (
  input  fenable,
  input  funct5,
  input  funct4,
  input  funct3,
  input  funct2,
  input  funct1,
  input  funct0,
  output add,
  output addu,
  output \and ,
  output sll,
  output sra,
  output srl,
  output sub,
  output \or ,
  output \nor ,
  output slt,
  output sltu,
  output jr,
  output srav
);

  wire and_1_out, and_2_out, and_3_out, and_4_out, and_5_out, and_6_out, and_7_out, and_8_out, and_9_out,
       and_10_out, and_11_out, and_12_out, and_13_out, not_1_out, not_2_out, not_3_out, not_4_out, not_5_out,
       not_6_out, not_7_out, not_8_out, not_9_out, not_10_out, not_11_out, not_12_out, not_13_out,
       not_14_out, not_15_out, not_16_out, not_17_out, not_18_out, not_19_out, not_20_out, not_21_out,
       not_22_out, not_23_out, not_24_out, not_25_out, not_26_out, not_27_out, not_28_out, not_29_out,
       not_30_out, not_31_out, not_32_out, not_33_out, not_34_out, not_35_out, not_36_out, not_37_out,
       not_38_out, not_39_out, not_40_out, not_41_out, not_42_out, not_43_out, not_44_out, not_45_out,
       not_46_out, not_47_out, not_48_out, not_49_out, not_50_out;

  not not_1 (not_1_out, funct4);
  not not_2 (not_2_out, funct3);
  not not_3 (not_3_out, funct2);
  not not_4 (not_4_out, funct1);
  not not_5 (not_5_out, funct0);
  not not_6 (not_6_out, funct4);
  not not_7 (not_7_out, funct3);
  not not_8 (not_8_out, funct2);
  not not_9 (not_9_out, funct1);
  not not_10 (not_10_out, funct4);
  not not_11 (not_11_out, funct3);
  not not_12 (not_12_out, funct1);
  not not_13 (not_13_out, funct0);
  not not_14 (not_14_out, funct5);
  not not_15 (not_15_out, funct4);
  not not_16 (not_16_out, funct3);
  not not_17 (not_17_out, funct2);
  not not_18 (not_18_out, funct1);
  not not_19 (not_19_out, funct0);
  not not_20 (not_20_out, funct5);
  not not_21 (not_21_out, funct4);
  not not_22 (not_22_out, funct3);
  not not_23 (not_23_out, funct2);
  not not_24 (not_24_out, funct5);
  not not_25 (not_25_out, funct4);
  not not_26 (not_26_out, funct3);
  not not_27 (not_27_out, funct2);
  not not_28 (not_28_out, funct0);
  not not_29 (not_29_out, funct4);
  not not_30 (not_30_out, funct3);
  not not_31 (not_31_out, funct2);
  not not_32 (not_32_out, funct0);
  not not_33 (not_33_out, funct4);
  not not_34 (not_34_out, funct3);
  not not_35 (not_35_out, funct1);
  not not_36 (not_36_out, funct4);
  not not_37 (not_37_out, funct3);
  not not_38 (not_38_out, funct4);
  not not_39 (not_39_out, funct2);
  not not_40 (not_40_out, funct0);
  not not_41 (not_41_out, funct4);
  not not_42 (not_42_out, funct2);
  not not_43 (not_43_out, funct5);
  not not_44 (not_44_out, funct4);
  not not_45 (not_45_out, funct2);
  not not_46 (not_46_out, funct1);
  not not_47 (not_47_out, funct0);
  not not_48 (not_48_out, funct5);
  not not_49 (not_49_out, funct4);
  not not_50 (not_50_out, funct3);
  and and_1 (and_1_out, funct5, not_1_out, not_2_out, not_3_out, not_4_out, not_5_out);
  and and_2 (and_2_out, funct5, not_6_out, not_7_out, not_8_out, not_9_out, funct0);
  and and_3 (and_3_out, funct5, not_10_out, not_11_out, funct2, not_12_out, not_13_out);
  and and_4 (and_4_out, not_14_out, not_15_out, not_16_out, not_17_out, not_18_out, not_19_out);
  and and_5 (and_5_out, not_20_out, not_21_out, not_22_out, not_23_out, funct1, funct0);
  and and_6 (and_6_out, not_24_out, not_25_out, not_26_out, not_27_out, funct1, not_28_out);
  and and_7 (and_7_out, funct5, not_29_out, not_30_out, not_31_out, funct1, not_32_out);
  and and_8 (and_8_out, funct5, not_33_out, not_34_out, funct2, not_35_out, funct0);
  and and_9 (and_9_out, funct5, not_36_out, not_37_out, funct2, funct1, funct0);
  and and_10 (and_10_out, funct5, not_38_out, funct3, not_39_out, funct1, not_40_out);
  and and_11 (and_11_out, funct5, not_41_out, funct3, not_42_out, funct1, funct0);
  and and_12 (and_12_out, not_43_out, not_44_out, funct3, not_45_out, not_46_out, not_47_out);
  and and_13 (and_13_out, not_48_out, not_49_out, not_50_out, funct2, funct1, funct0);
  and and_14 (add, fenable, and_1_out);
  and and_15 (addu, fenable, and_2_out);
  and and_16 (\and , fenable, and_3_out);
  and and_17 (sll, fenable, and_4_out);
  and and_18 (sra, fenable, and_5_out);
  and and_19 (srl, fenable, and_6_out);
  and and_20 (sub, fenable, and_7_out);
  and and_21 (\or , fenable, and_8_out);
  and and_22 (\nor , fenable, and_9_out);
  and and_23 (slt, fenable, and_10_out);
  and and_24 (sltu, fenable, and_11_out);
  and and_25 (jr, fenable, and_12_out);
  and and_26 (srav, fenable, and_13_out);
endmodule
